# Fritzing sketch FJXZCA6J0486PZ4 (saved by Fritzing 0.9.3b)
circuit board: 10.3908cm x 1.8cm
breadboards: 1

parts:
  OLED_I2C1 = OLED 128x64 I2C Monochrome Display
  S1 = JOYSTICK_MINI [package=joystick_mini]
  R8 = Resistor [tolerance=±5% resistance=22k package="0805 [SMD]"]
  R11 = Resistor [tolerance=±5% resistance=47k package="0805 [SMD]"]
  R9 = Resistor [tolerance=±5% resistance=68k package="0805 [SMD]"]
  R7 = Resistor [tolerance=±5% resistance=10k package="0805 [SMD]"]
  R12 = Resistor [tolerance=±5% resistance=100k package="0805 [SMD]"]
  R10 = Resistor [tolerance=±5% resistance=80k package="0805 [SMD]"]
  IC1 = 24LC01 [package="SO8 [SMD]"]
  Pad4 = Pad [width=11.4 height=1.5 connect=center]  # not connected
  Pad3 = Pad [width=11.4 height=1.5 connect=center]  # not connected
  Pad2 = Pad [width=11.4 height=1.5 connect=center]  # not connected
  Pad1 = Pad [width=11.4 height=1.5 connect=center]  # not connected
  SparkFun_Pro_Micro1 = SparkFun Pro Micro [part_number=DEV-12640]

nets:
  N1: OLED_I2C1.SDA, IC1.SDA_-_I2C_Data, SparkFun_Pro_Micro1.D2
  N2: OLED_I2C1.SCK, IC1.SCL_-_I2C_Clock, SparkFun_Pro_Micro1.D3
  5V: OLED_I2C1.VDD, R8.Pin_1, R11.Pin_1, R9.Pin_1, R7.Pin_1, R10.Pin_1, IC1.+V, SparkFun_Pro_Micro1.VCC
  GND: OLED_I2C1.GND, R12.Pin_0, IC1.A0, IC1.A1, IC1.A2, IC1.0V, IC1.WP_-_Write_Protect, SparkFun_Pro_Micro1.GND
  N3: S1.UP, R10.Pin_0
  N4: S1.RIGHT, R9.Pin_0
  N5: S1.LEFT, R11.Pin_0
  N6: S1.CENT, R8.Pin_0
  N7: S1.DOWN, R7.Pin_0
  N8: S1.GND, R12.Pin_1, SparkFun_Pro_Micro1.A3

notes:
  80k
  22k
  47k
  68k
  10k
  100k

custom parts:
  SparkFun Pro Micro: This tiny little board does all of the neat-o Arduino tricks that you’re familiar with: 4 channels of 10-bit ADC, 5 PWM pins, 12 DIOs as well as hardware serial connections Rx and Tx. Running at 16MHz and 5V, this board will remind you a lot of your other favorite Arduino-compatible boards but this little guy can go just about anywhere. There is a voltage regulator on board so it can accept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
